// Logisim project Project2.circ as structural Verilog
module main (
  input  in_1,
  input  in_2,
  input  in_3,
  input  in_4,
  input  in_5,
  input  in_6,
  input  in_7,
  input  in_8,
  input  in_9,
  input  in_10,
  input  in_11
);

  DotMatrix #(.matrixcols(3), .matrixrows(5)) dotmatrix_1 ();  // open: col0, col1, col2
  DotMatrix #(.matrixcols(3), .matrixrows(5)) dotmatrix_2 ();  // open: col0, col1, col2
  DotMatrix #(.matrixcols(3), .matrixrows(5)) dotmatrix_3 ();  // open: col0, col1, col2
  DotMatrix #(.matrixcols(3), .matrixrows(5)) dotmatrix_4 ();  // open: col0, col1, col2
  DotMatrix #(.matrixcols(3), .matrixrows(5)) dotmatrix_5 ();  // open: col0, col1, col2
  DotMatrix #(.matrixcols(3), .matrixrows(5)) dotmatrix_6 ();  // open: col0, col1, col2
  DotMatrix #(.matrixcols(3), .matrixrows(5)) dotmatrix_7 ();  // open: col0, col1, col2
  DotMatrix #(.matrixcols(3), .matrixrows(5)) dotmatrix_8 ();  // open: col0, col1, col2
  DotMatrix #(.matrixcols(3), .matrixrows(5)) dotmatrix_9 ();  // open: col0, col1, col2
endmodule
