// Logisim project proj2.circ as structural Verilog: 3 circuits, main circuit 4-Bit-Adder
// 1
module _4_Bit_Adder (
  input  _1,
  input  _2,
  input  _1_2,
  input  _2_2,
  input  in_5,
  output out_6,
  output out_7,
  output out_8
);

  wire and_1_out, and_2_out, and_3_out, and_4_out, or_1_out, xor_1_out, xor_2_out;

  xor xor_1 (xor_1_out, _1, _1_2);
  and and_1 (and_1_out, _1, _1_2);
  xor xor_2 (xor_2_out, _2, _2_2);
  and and_2 (and_2_out, _2, _2_2);
  xor xor_3 (out_8, in_5, xor_1_out);
  and and_3 (and_3_out, in_5, xor_1_out);
  xor xor_4 (out_7, or_1_out, xor_2_out);
  and and_4 (and_4_out, or_1_out, xor_2_out);
  or or_1 (or_1_out, and_3_out, and_1_out);
  or or_2 (out_6, and_4_out, and_2_out);
endmodule

module Main_Circuit (
  input  in_1,
  input  in_2,
  input  in_3,
  input  in_4
);

  wire n4_bit_adder_1_out_6, n4_bit_adder_1_out_7, n4_bit_adder_1_out_8;
  wire [4:0] led_controler_1_out_2, led_controler_1_out_3, led_controler_1_out_4, led_controler_2_out_2,
       led_controler_2_out_3, led_controler_2_out_4, led_controler_3_out_2, led_controler_3_out_3,
       led_controler_3_out_4, led_controler_4_out_2, led_controler_4_out_3, led_controler_4_out_4,
       led_controler_5_out_2, led_controler_5_out_3, led_controler_5_out_4, led_controler_6_out_2,
       led_controler_6_out_3, led_controler_6_out_4, led_controler_7_out_2, led_controler_7_out_3,
       led_controler_7_out_4;

  DotMatrix #(.matrixcols(3), .matrixrows(5)) dotmatrix_1 (
    .col0(led_controler_1_out_2), .col1(led_controler_1_out_3), .col2(led_controler_1_out_4));
  LED_Controler led_controler_1 (
    .out_2(led_controler_1_out_2), .out_3(led_controler_1_out_3), .out_4(led_controler_1_out_4), .in_1(in_1));
  DotMatrix #(.matrixcols(3), .matrixrows(5)) dotmatrix_2 (
    .col0(led_controler_3_out_2), .col1(led_controler_3_out_3), .col2(led_controler_3_out_4));
  DotMatrix #(.matrixcols(3), .matrixrows(5)) dotmatrix_3 (
    .col0(led_controler_2_out_2), .col1(led_controler_2_out_3), .col2(led_controler_2_out_4));
  LED_Controler led_controler_2 (
    .out_2(led_controler_2_out_2), .out_3(led_controler_2_out_3), .out_4(led_controler_2_out_4), .in_1(in_2));
  LED_Controler led_controler_3 (
    .out_2(led_controler_3_out_2), .out_3(led_controler_3_out_3), .out_4(led_controler_3_out_4), .in_1(in_3));
  DotMatrix #(.matrixcols(3), .matrixrows(5)) dotmatrix_4 (
    .col0(led_controler_4_out_2), .col1(led_controler_4_out_3), .col2(led_controler_4_out_4));
  DotMatrix #(.matrixcols(3), .matrixrows(5)) dotmatrix_5 (
    .col0(led_controler_5_out_2), .col1(led_controler_5_out_3), .col2(led_controler_5_out_4));
  LED_Controler led_controler_4 (
    .out_2(led_controler_4_out_2), .out_3(led_controler_4_out_3), .out_4(led_controler_4_out_4), .in_1(in_4));
  LED_Controler led_controler_5 (
    .out_2(led_controler_5_out_2), .out_3(led_controler_5_out_3), .out_4(led_controler_5_out_4),
    .in_1(n4_bit_adder_1_out_6));
  _4_Bit_Adder u_4_bit_adder_1 (
    .in_5(1'b0), ._1(in_2), ._2(in_1), ._1_2(in_4), ._2_2(in_3), .out_6(n4_bit_adder_1_out_6),
    .out_7(n4_bit_adder_1_out_7), .out_8(n4_bit_adder_1_out_8));
  DotMatrix #(.matrixcols(3), .matrixrows(5)) dotmatrix_6 (
    .col0(led_controler_7_out_2), .col1(led_controler_7_out_3), .col2(led_controler_7_out_4));
  DotMatrix #(.matrixcols(3), .matrixrows(5)) dotmatrix_7 (
    .col0(led_controler_6_out_2), .col1(led_controler_6_out_3), .col2(led_controler_6_out_4));
  LED_Controler led_controler_6 (
    .out_2(led_controler_6_out_2), .out_3(led_controler_6_out_3), .out_4(led_controler_6_out_4),
    .in_1(n4_bit_adder_1_out_8));
  LED_Controler led_controler_7 (
    .out_2(led_controler_7_out_2), .out_3(led_controler_7_out_3), .out_4(led_controler_7_out_4),
    .in_1(n4_bit_adder_1_out_7));
endmodule

module LED_Controler (
  input  in_1,
  output [4:0] out_2,
  output [4:0] out_3,
  output [4:0] out_4
);

  not not_1 (out_2[3], in_1);
  not not_2 (out_4[4], in_1);

  assign {out_2[4], out_2[2:0]} = {1'b1, {2{out_2[3]}}, 1'b1};
  assign out_3 = {1'b1, {3{in_1}}, 1'b1};
  assign out_4[3:0] = {{3{out_4[4]}}, 1'b1};
endmodule
